# Fritzing sketch Project 2 (saved by Fritzing 0.9.3b)

parts:
  Part1 = Arduino Ethernet Shield (Rev3)
  hc-sr1 = hc-sr04
  Part2 = Soil Moisture Sensor
  U1 = GS406SMD [package=gs406smd]  # not connected
  Part3 = Bluetooth HC-05 Macho
  VCC1 = Battery block 9V

nets:
  N1: Part1.PWM_D11, Part2.SIG
  N2: Part1.SPI/D12, hc-sr1.Echo
  N3: Part1.SPI/D13, hc-sr1.Trig
  GND: Part1.GND, hc-sr1.GND, Part2.GND, VCC1.-
  N4: Part1.RX/D0, Part3.TXD
  N5: Part1.TX/D1, Part3.RXD
  5V: Part1.5V, Part3.VCC
  N6: Part1.VIN, VCC1.+

// code stored in the sketch: Untitled2.ino
#include <SoftwareSerial.h>
#include <TinyGPS++.h>

// Pin definitions
const int trigPin = 9; // Ultrasonic sensor trigger pin
const int echoPin = 10; // Ultrasonic sensor echo pin
const int moistureSensorPin = A0; // Soil moisture sensor pin
const int gpsRXPin = 4; // GPS RX pin
const int gpsTXPin = 3; // GPS TX pin

// Variables
int moistureValue = 0;
long duration;
int distance;

// Create a GPS instance
TinyGPSPlus gps;
SoftwareSerial gpsSerial(gpsRXPin, gpsTXPin); // RX, TX for GPS

void setup() {
  Serial.begin(9600);       // For communication with PC
  gpsSerial.begin(9600);    // For communication with GPS module

  pinMode(trigPin, OUTPUT);
  pinMode(echoPin, INPUT);
  pinMode(moistureSensorPin, INPUT);
}

void loop() {
  // Measure moisture (wet/dry detection)
  moistureValue = analogRead(moistureSensorPin);
  if (moistureValue < 400) {
    Serial.println("Dry Waste Detected");
  } else {
    Serial.println("Wet Waste Detected");
  }

  // Measure distance using ultrasonic sensor (fill level detection)
  digitalWrite(trigPin, LOW);
  delayMicroseconds(2);
  digitalWrite(trigPin, HIGH);
  delayMicroseconds(10);
  digitalWrite(trigPin, LOW);
  
  duration = pulseIn(echoPin, HIGH);
  distance = duration * 0.034 / 2;
  
  // Assuming bin height is 30 cm, adjust as per your dustbin
  if (distance < 5) {
    Serial.println("Dustbin is Full");
  } else {
    Serial.print("Distance to Waste: ");
    Serial.print(distance);
    Serial.println(" cm");
  }

  // GPS Data
  while (gpsSerial.available() > 0) {
    gps.encode(gpsSerial.read());
    
    if (gps.location.isUpdated()) {
      Serial.print("Latitude: ");
      Serial.println(gps.location.lat(), 6);
      Serial.print("Longitude: ");
      Serial.println(gps.location.lng(), 6);
    }
  }

  delay(2000); // Wait for 2 seconds before next reading
}
